// Digital circuit GPR.dig as structural Verilog
module GPR (
  input  [1:0] pick_register,
  input  ctrl,
  input  [7:0] \input ,
  input  clk,
  output [7:0] Output
);

  wire and_1_out, and_2_out, and_3_out, and_4_out, decoder_1_out_0, decoder_1_out_1, decoder_1_out_2,
       decoder_1_out_3;
  wire [7:0] register_1_q, register_2_q, register_3_q, register_4_q;

  Decoder #(.Selector_Bits(2)) decoder_1 (
    .sel(pick_register), .out_0(decoder_1_out_0), .out_1(decoder_1_out_1), .out_2(decoder_1_out_2),
    .out_3(decoder_1_out_3));
  and and_1 (and_1_out, decoder_1_out_0, clk);
  and and_2 (and_2_out, decoder_1_out_1, clk);
  and and_3 (and_3_out, decoder_1_out_2, clk);
  and and_4 (and_4_out, clk, decoder_1_out_3);
  Register #(.Bits(8)) register_1 (.D(\input ), .C(ctrl), .en(and_1_out), .Q(register_1_q));
  Register #(.Bits(8)) register_2 (.D(\input ), .C(ctrl), .en(and_2_out), .Q(register_2_q));
  Register #(.Bits(8)) register_3 (.D(\input ), .C(ctrl), .en(and_3_out), .Q(register_3_q));
  Register #(.Bits(8)) register_4 (.D(\input ), .C(ctrl), .en(and_4_out), .Q(register_4_q));
  Multiplexer #(.Selector_Bits(2), .Bits(8)) multiplexer_1 (
    .sel(pick_register), .in_0(register_1_q), .in_1(register_2_q), .in_2(register_3_q), .in_3(register_4_q),
    .out(Output));
endmodule
