// Digital circuit IR.dig as structural Verilog
module IR (
  input  [7:0] D_IN,
  input  LD,
  input  CLK,
  output [7:0] D_OUT
);

  wire [7:0] multiplexer_1_out;

  Multiplexer #(.Bits(8)) multiplexer_1 (.sel(LD), .in_0(D_IN), .in_1({8{1'b0}}), .out(multiplexer_1_out));
  Register #(.Bits(8)) IR (.D(multiplexer_1_out), .C(CLK), .en(LD), .Q(D_OUT));
endmodule
