// Digital circuit PC.dig as structural Verilog
module PC (
  input  [1:0] ctrl,
  input  clk,
  input  [7:0] carry,
  output [7:0] \output 
);

  wire [7:0] adder_1_c, multiplexer_1_out;

  Adder adder_1 (.A({\output [7:1], \output [2]}), .B(carry), .C_IN(1'b0), .C(adder_1_c));  // open: C_OUT
  Multiplexer #(.Selector_Bits(2), .Bits(8)) multiplexer_1 (
    .sel(ctrl), .in_0({\output [7:1], \output [2]}), .in_1(adder_1_c), .in_2({8{1'b0}}), .in_3({8{1'b1}}),
    .out(multiplexer_1_out));
  D_FF d_ff_1 (.D(multiplexer_1_out[7]), .C(clk), .Q(\output [7]));  // open: nQ
  D_FF d_ff_2 (.D(multiplexer_1_out[6]), .C(clk), .Q(\output [6]));  // open: nQ
  D_FF d_ff_3 (.D(multiplexer_1_out[5]), .C(clk), .Q(\output [5]));  // open: nQ
  D_FF d_ff_4 (.D(multiplexer_1_out[4]), .C(clk), .Q(\output [4]));  // open: nQ
  D_FF d_ff_5 (.D(multiplexer_1_out[3]), .C(clk), .Q(\output [3]));  // open: nQ
  D_FF d_ff_6 (.D(multiplexer_1_out[2]), .C(clk), .Q(\output [2]));  // open: nQ
  D_FF d_ff_7 (.D(multiplexer_1_out[1]), .C(clk), .Q(\output [1]));  // open: nQ
  D_FF d_ff_8 (.D(multiplexer_1_out[0]), .C(clk), .Q(\output [2]));  // open: nQ

  assign \output [0] = \output [2];

  // Notes on the sheet:
  //   ctrl: 00->Load
  //   01->Store
  //   10->Clear
  //   11->Set FF
endmodule
