// Digital circuit Register.dig as structural Verilog
module Register (
  input  [1:0] pick_register,
  input  ctrl,
  input  [7:0] \input ,
  input  clk,
  output [7:0] \output 
);

  wire and_1_out, and_2_out, and_3_out, and_4_out, decoder_1_out_0, decoder_1_out_1, decoder_1_out_2,
       decoder_1_out_3;
  wire [7:0] R0_q, R1_q, R2_q, R3_q;

  Decoder #(.Selector_Bits(2)) decoder_1 (
    .sel(pick_register), .out_0(decoder_1_out_0), .out_1(decoder_1_out_1), .out_2(decoder_1_out_2),
    .out_3(decoder_1_out_3));
  and and_1 (and_1_out, decoder_1_out_0, clk);
  and and_2 (and_2_out, decoder_1_out_1, clk);
  and and_3 (and_3_out, decoder_1_out_2, clk);
  and and_4 (and_4_out, decoder_1_out_3, clk);
  Register #(.Bits(8), .isProgramCounter("true")) R0 (.D(\input ), .C(ctrl), .en(and_1_out), .Q(R0_q));
  Register #(.Bits(8), .isProgramCounter("true")) R1 (.D(\input ), .C(ctrl), .en(and_2_out), .Q(R1_q));
  Register #(.Bits(8), .isProgramCounter("true")) R2 (.D(\input ), .C(ctrl), .en(and_3_out), .Q(R2_q));
  Register #(.Bits(8), .isProgramCounter("true")) R3 (.D(\input ), .C(ctrl), .en(and_4_out), .Q(R3_q));
  Multiplexer #(.Selector_Bits(2), .Bits(8)) multiplexer_1 (
    .sel(pick_register), .in_0(R0_q), .in_1(R1_q), .in_2(R2_q), .in_3(R3_q), .out(\output ));
endmodule
