// Digital circuit RegisterSRAM.dig as structural Verilog
module RegisterSRAM (
  input  Clock,
  input  [1:0] PC_INC,
  input  OE,
  input  CS,
  input  WE,
  input  GPR_LD,
  input  IR_LD
);

  wire [7:0] gpr_1_output, PC_output, sram_1_d_out;

  PC PC (.ctrl(PC_INC), .clk(Clock), .\output (PC_output));  // open: carry
  GPR gpr_1 (.ctrl(GPR_LD), .\input (sram_1_d_out), .clk(Clock), .Output(gpr_1_output));  // open: pick_register
  SRAM sram_1 (.ADDRESS(PC_output[3:0]), .D_IN(gpr_1_output), .WE(WE), .CS(CS), .OE(OE), .D_OUT(sram_1_d_out));
  IR ir_1 (.D_IN(sram_1_d_out), .LD(IR_LD), .CLK(Clock));  // open: D_OUT
  // Pins of 1 and 2 bits meet at PC_INC
endmodule
