// Digital circuit SRAM.dig as structural Verilog
module SRAM (
  input  [3:0] ADDRESS,
  input  [7:0] D_IN,
  input  WE,
  input  CS,
  input  OE,
  output [7:0] D_OUT
);

  RAMSinglePortSel #(.AddrBits(4), .Bits(8)) SRAM (.A(ADDRESS), .CS(CS), .WE(WE), .OE(OE), .D(D_OUT));
endmodule
